// Logisim project ALU.circ as structural Verilog: 1 circuit, main circuit main
module main (
  input  no,
  input  zx,
  input  nx,
  input  f,
  input  [15:0] in_5,
  input  [15:0] x,
  input  zy,
  input  ny,
  input  [15:0] y,
  input  [15:0] in_10,
  output [15:0] out_11,
  output zr,
  output ng
);

  wire [15:0] multiplexer_1_out, multiplexer_2_out, multiplexer_3_out, multiplexer_4_out, not_2_out,
       not_3_out;

  // NOT_Gate not_1 is placed but not wired
  BitAdder bitadder_1 ();  // open: in0, out
  Multiplexer #(.width(16)) multiplexer_1 (.in0(x), .in1(in_5), .out(multiplexer_1_out), .sel(zx));
  Multiplexer #(.width(16)) multiplexer_2 (.in0(y), .in1(in_10), .out(multiplexer_2_out), .sel(zy));
  assign not_2_out = ~multiplexer_1_out;  // NOT_Gate not_2, 16 bits wide
  assign not_3_out = ~multiplexer_2_out;  // NOT_Gate not_3, 16 bits wide
  Multiplexer #(.width(16)) multiplexer_3 (.in0(multiplexer_1_out), .in1(not_2_out), .out(multiplexer_3_out), .sel(nx));
  Multiplexer #(.width(16)) multiplexer_4 (.in0(multiplexer_2_out), .in1(not_3_out), .out(multiplexer_4_out), .sel(ny));
  // NOT_Gate not_4 is placed but not wired
endmodule
