// Logisim project DMux.circ as structural Verilog: 1 circuit, main circuit main
module main (
  input  inp,
  input  sel
);

  wire and_1_out, and_2_out, not_1_out;

  not not_1 (not_1_out, sel);
  and and_1 (and_1_out, inp, not_1_out);
  and and_2 (and_2_out, sel, inp);
  LED a (.in(and_1_out));
  LED b (.in(and_2_out));
endmodule
